# Fritzing sketch MIDI Relay (saved by Fritzing 0.9.4)

parts:
  Part1 = Arduino Mega 2560 (Rev3)
  Part2 = Arduino Midi Shield
  8_Channel_Relay1 = 8 Channel Power Relay
  8_Channel_Relay2 = 8 Channel Power Relay
  8_Channel_Relay3 = 8 Channel Power Relay

nets:
  N1: Part1.D19/RX1, Part2.RX-I
  N2: Part1.D18/TX1, Part2.TX
  GND: Part1.GND, Part2.GND, 8_Channel_Relay1.GND, 8_Channel_Relay2.GND, 8_Channel_Relay3.GND
  VCC: Part1.5V, Part2.VCC, 8_Channel_Relay1.VCC, 8_Channel_Relay2.VCC, 8_Channel_Relay3.VCC
  N3: Part1.D26, 8_Channel_Relay1.IN1
  N4: Part1.D27, 8_Channel_Relay1.IN2
  N5: Part1.D28, 8_Channel_Relay1.IN3
  N6: Part1.D29, 8_Channel_Relay1.IN4
  N7: Part1.D30, 8_Channel_Relay1.IN5
  N8: Part1.D31, 8_Channel_Relay1.IN6
  N9: Part1.D32, 8_Channel_Relay1.IN7
  N10: Part1.D33, 8_Channel_Relay1.IN8
  N11: Part1.D34, 8_Channel_Relay2.IN1
  N12: Part1.D35, 8_Channel_Relay2.IN2
  N13: Part1.D36, 8_Channel_Relay2.IN3
  N14: Part1.D37, 8_Channel_Relay2.IN4
  N15: Part1.D38, 8_Channel_Relay2.IN5
  N16: Part1.D39, 8_Channel_Relay2.IN6
  N17: Part1.D40, 8_Channel_Relay2.IN7
  N18: Part1.D41, 8_Channel_Relay2.IN8
  N19: Part1.D42, 8_Channel_Relay3.IN1
  N20: Part1.D43, 8_Channel_Relay3.IN2
  N21: Part1.D44, 8_Channel_Relay3.IN3
  N22: Part1.D45, 8_Channel_Relay3.IN4
  N23: Part1.D46, 8_Channel_Relay3.IN5
  N24: Part1.D47, 8_Channel_Relay3.IN6
  N25: Part1.D48, 8_Channel_Relay3.IN7
  N26: Part1.D49, 8_Channel_Relay3.IN8

custom parts:
  8 Channel Power Relay: An 8 channel power relay. The module operates at 5V.
